# Fritzing sketch Schematics Data 2024 (saved by Fritzing 1.0.2b)

parts:
  PDH1 = rev_pdh
  Kraken1 = Kraken-Right
  ctrl1 = rev_spark_max [part_number=rev-11-2158]
  BLDC1 = REV NEO 550 BLDC Motor [part_number=REV-21-1651]
  BLDC2 = REV NEO 550 BLDC Motor [part_number=REV-21-1651]
  ctrl1_2 = rev_spark_max [part_number=rev-11-2158]
  cntl1 = roborio1
  BLDC3 = CTRE Falcon 500 [part_number=19-708850]
  CANConnectorS1 = CAN Connector - Small
  R1 = Resistor [tolerance=±5% power=0.25W resistance=220 package=THT]
  Falcon1 = Falcon_Left1
  Vortex3 = NEO Vortex
  Kraken2 = Kraken- Left1
  Kraken3 = Kraken- Left1
  Kraken4 = Kraken- Left1
  R2 = Resistor [tolerance=±5% power=0.25W resistance=220 package=THT]
  CANivore1 = CTRE CANivore [form="♀ (female)" package=THT]
  Pigeon_2_1 = CTRE Pigeon 2.0 [package=THT]
  switch1 = Network Switch
  J1 = Generic female header - 5 pins [form="♀ (female)" package=THT]
  RPM1 = rev_rpm
  Router1 = Rounter OpenMesh
  TBE1 = REV Through Bore Encoder
  J2 = Generic female header - 3 pins [form="♀ (female)" package=THT]
  J3 = Generic female header - 1 pins [form="♀ (female)" package=THT]
  J4 = Generic female header - 1 pins [form="♀ (female)" package=THT]  # not connected
  J5 = Generic female header - 1 pins [form="♀ (female)" package=THT]
  J6 = Generic female header - 1 pins [form="♀ (female)" package=THT]
  J7 = OrangePi  # not connected
  J8 = Generic female header - 1 pins [form="♀ (female)" package=THT]
  J9 = Generic female header - 1 pins [form="♀ (female)" package=THT]  # not connected
  J10 = Generic female header - 2 pins [form="♀ (female)" package=THT]
  J11 = Generic female header - 2 pins [form="♀ (female)" package=THT]
  Kraken7 = Kraken- Left1
  BLDC6 = CTRE Falcon 500 [part_number=19-708850]
  Kraken8 = Kraken- Left1
  BLDC7 = CTRE Falcon 500 [part_number=19-708850]
  Kraken9 = Kraken- Left1
  BLDC8 = CTRE Falcon 500 [part_number=19-708850]
  Kraken10 = Kraken- Left1
  BLDC9 = CTRE Falcon 500 [part_number=19-708850]
  R3 = Resistor [tolerance=±5% power=0.25W resistance=220 package=THT]
  Vortex4 = NEO Vortex
  RSL1 = FRC Robot Signal Light [part_number=855PB-B12ME522]
  Vortex5 = NEO Vortex
  CANcoder1 = CTRE CANcoder [package=THT]
  CANcoder2 = CTRE CANcoder [package=THT]
  CANcoder3 = CTRE CANcoder [package=THT]
  CANcoder4 = CTRE CANcoder [package=THT]
  U1 = SK6812 RGBW LED Strip

nets:
  N1: PDH1.connector40, Kraken1.CAN_Low2
  N2: PDH1.connector41, Kraken1.CAN-High2
  N3: PDH1.connector42, Falcon1.CAN_Low_1
  N4: PDH1.connector43, Falcon1.CAN_High_1
  N5: Kraken1.CAN_High1, CANConnectorS1.CAN_HighOut, Vortex4.CAN-Low1
  N6: Kraken1.CAN_Low1, CANConnectorS1.CAN_LowOut, Vortex4.CAN-High1
  N7: ctrl1.connector4, Vortex5.CAN-Low1
  N8: ctrl1.connector5, Vortex5.CAN-High1
  N9: ctrl1.connector6, ctrl1_2.connector4
  N10: ctrl1.connector7, ctrl1_2.connector5
  N11: ctrl1.connector19, BLDC1.GND
  N12: BLDC2.GND, ctrl1_2.connector19
  N13: ctrl1_2.connector6, cntl1.connector1
  N14: ctrl1_2.connector7, cntl1.connector0
  N15: cntl1.connector9, TBE1.GND
  N16: cntl1.connector10, TBE1.A
  N17: cntl1.connector11, TBE1.V
  N18: cntl1.connector12, J2.GND
  N19: cntl1.connector14, J2.V+, J2.Out
  N20: cntl1.connector15, J10.-
  N21: cntl1.connector17, J10.+
  N22: cntl1.connector18, J11.-
  N23: cntl1.connector20, J11.+
  N24: cntl1.connector41, RSL1.anode0
  N25: cntl1.connector42, RSL1.common_cathode
  N26: cntl1.connector111, U1.+5V
  N27: cntl1.connector112, U1.Din, U1.GND#3
  N28: cntl1.connector113, U1.GND#0
  N29: cntl1.connector142, CANivore1.USB-C
  N30: cntl1.connector144, switch1.pin1
  N31: BLDC3.CANL0, R1.Pin_1
  N32: BLDC3.CANH1#3, R1.Pin_0
  N33: BLDC3.CANL1, Vortex4.-
  N34: BLDC3.CANH1#5, Vortex4.+
  N35: CANConnectorS1.CAN_HighIn, Vortex5.+
  N36: CANConnectorS1.CAN_LowIn, Vortex5.-
  N37: Falcon1.CAN_High_2, Vortex3.+
  N38: Falcon1.CAN_Low_2, Vortex3.-
  N39: Vortex3.CAN-Low1, Kraken3.CAN_High_2
  N40: Vortex3.CAN-High1, Kraken3.CAN_Low_2
  N41: Kraken2.CAN_High_1, Kraken4.CAN_High_2
  N42: Kraken2.CAN_Low_1, Kraken4.CAN_Low_2
  N43: Kraken2.CAN_High_2, Kraken3.CAN_High_1
  N44: Kraken2.CAN_Low_2, Kraken3.CAN_Low_1
  N45: Kraken4.CAN_High_1, R2.Pin_1
  N46: Kraken4.CAN_Low_1, R2.Pin_0
  N47: CANivore1.CANL[G], Kraken9.CAN_Low_2
  N48: CANivore1.CANH[Y], Kraken9.CAN_High_2
  N49: Pigeon_2_1.IN-CANH[Y], BLDC7.CANH1#3
  N50: Pigeon_2_1.IN-CANL[G], BLDC7.CANL0
  N51: Pigeon_2_1.OUT-CANH[Y], Kraken7.CAN_High_2
  N52: Pigeon_2_1.OUT-CANL[G], Kraken7.CAN_Low_2
  N53: switch1.pin3, J1.Ethernet
  N54: switch1.pin5, RPM1.connector3
  N55: J1.USB-1, J5.pin1
  N56: J1.USB-2, J3.pin1
  N57: J1.USB-3, J8.pin1
  N58: J1.USB-4, J6.pin1
  N59: RPM1.connector2, Router1.ETH_right
  N60: Kraken7.CAN_High_1, CANcoder3.OUT-CANH[Y]
  N61: Kraken7.CAN_Low_1, BLDC6.CANL0, Kraken10.CAN_Low_2, CANcoder3.OUT-CANL[G]
  N62: BLDC6.CANH1#3, Kraken10.CAN_High_2
  N63: BLDC6.CANL1, CANcoder3.IN-CANL[G]
  N64: BLDC6.CANH1#5, CANcoder3.IN-CANH[Y]
  N65: Kraken8.CAN_High_1, CANcoder2.OUT-CANH[Y]
  N66: Kraken8.CAN_Low_1, CANcoder2.OUT-CANL[G]
  N67: Kraken8.CAN_High_2, BLDC8.CANH1#3
  N68: Kraken8.CAN_Low_2, BLDC8.CANL0
  N69: BLDC7.CANL1, CANcoder2.IN-CANL[G]
  N70: BLDC7.CANH1#5, CANcoder2.IN-CANH[Y]
  N71: Kraken9.CAN_High_1, CANcoder1.OUT-CANH[Y]
  N72: Kraken9.CAN_Low_1, CANcoder1.OUT-CANL[G]
  N73: BLDC8.CANL1, CANcoder1.IN-CANL[G]
  N74: BLDC8.CANH1#5, CANcoder1.IN-CANH[Y]
  N75: Kraken10.CAN_High_1, CANcoder4.OUT-CANH[Y]
  N76: Kraken10.CAN_Low_1, CANcoder4.OUT-CANL[G]
  N77: BLDC9.CANL0, R3.Pin_0
  N78: BLDC9.CANH1#3, R3.Pin_1
  N79: BLDC9.CANL1, CANcoder4.IN-CANL[G]
  N80: BLDC9.CANH1#5, CANcoder4.IN-CANH[Y]

custom parts:
  Kraken-Right: Kraken
  REV NEO 550 BLDC Motor: The REV NEO 550 Brushless Motor is the newest member in the NEO family of brushless motors. Its output power and small size are specifically designed to make NEO 550 the perfect motor for intakes and other non-drivetrain robot mechanisms. Mounting holes and pilot match a standard 550 series motor, making it natively mount to many existing off-the-shelf gearboxes.
  CTRE Falcon 500: The Falcon 500 powered by Talon FX is a brushless motor with an integrated motor controller and high-resolution encoder, custom designed specifically for the FIRST Robotics Competition, through a collaboration between Cross the Road Electronics and VEX Robotics.
  CAN Connector - Small: Made for CAN Paths on Fritzing
  Falcon_Left1: Falcon
  Kraken- Left1: Kraken
  CTRE Pigeon 2.0: Generic single row SMD female header
  Generic female header - 5 pins: Generic female header
  REV Through Bore Encoder: The REV Through Bore Encoder is specifically designed with the end user in mind, allowing teams to place sensors in the locations closest to the rotation that they wish to measure. This rotary sensor measures both relative and absolute position through its ABI quadrature output and its absolute position pulse output. Mounting an encoder has never been easier with a 1/2in Hex Through Bore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
  Generic female header - 3 pins: Generic female header
  Generic female header - 1 pins: Generic female header
  Generic female header - 2 pins: Generic female header
  FRC Robot Signal Light: Panel Mount Beacon,12V AC/DC,45 mm Panel Mounting LED,Amber,22.5 mm Round Mounting Hole Used as: R709 *ROBOTS must have a signal light. ROBOTS must use at least 1, but no more than 2, diagnostic ROBOT Signal Light (RSL) (P/N 855PB-B12ME522). Any RSL must be: A. mounted on the ROBOT such that it is easily visible while standing 3 ft. (~ 100 cm) in front of the ROBOT, B. connected to the “RSL”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
  SK6812 RGBW LED Strip: SK6812 RGBW Strip
