# Fritzing sketch Schematics Power 2024 (saved by Fritzing 1.0.2b)

parts:
  PDH1 = rev_pdh
  Kraken1 = Kraken1
  Kraken2 = Kraken-Right
  Kraken3 = Kraken-Right
  Kraken4 = Kraken-Right
  Kraken5 = Kraken-Right
  Falcon1 = Falcon_Left1
  BLDC1 = CTRE Falcon 500 [part_number=19-708850]
  BLDC2 = CTRE Falcon 500 [part_number=19-708850]
  BLDC3 = CTRE Falcon 500 [part_number=19-708850]
  Falcon2 = Falcon_Left1
  Falcon3 = Falcon_Left1
  Kraken6 = Kraken1
  Kraken7 = Kraken1
  Kraken8 = Kraken1
  ctrl1 = rev_spark_max [part_number=rev-11-2158]
  ctrl2 = rev_spark_max [part_number=rev-11-2158]
  BLDC4 = REV NEO 550 BLDC Motor [part_number=REV-21-1651]
  BLDC5 = REV NEO 550 BLDC Motor [part_number=REV-21-1651]
  Vortex1 = NEO Vortex
  Vortex2 = NEO Vortex
  Vortex3 = NEO Vortex
  BAT1 = Battery 12V [package=battcom_20mm_pth]
  switch1 = Network Switch
  RPM1 = rev_rpm
  J1 = Generic female header - 2 pins [form="♀ (female)" package=THT]
  cntl1 = roborio1
  Mini_Power_Module1 = REV Mini Power Module [form="♀ (female)" package=THT]
  J2 = Generic female header - 5 pins [form="♀ (female)" package=THT]
  BuckBoost1 = Beelink BuckBoost
  J3 = Buckboostpi
  J4 = OrangePi
  Pigeon_2_1 = CTRE Pigeon 2.0 [package=THT]
  CANivore1 = CTRE CANivore [form="♀ (female)" package=THT]
  CANcoder1 = CTRE CANcoder [package=THT]
  CANcoder2 = CTRE CANcoder [package=THT]
  CANcoder3 = CTRE CANcoder [package=THT]
  CANcoder4 = CTRE CANcoder [package=THT]
  Part1 = Wago 222
  Part2 = Wago 222
  Part3 = Wago 222
  Part4 = Wago 222
  JP1 = APP SB50 [package=sb50]
  JP2 = APP SB50 [package=sb50]
  CB1 = Thermal Circuit Breaker [package=waterproof]
  Part5 = Wago 222  # not connected

nets:
  N1: PDH1.connector0, Kraken5.+
  N2: PDH1.connector1, Kraken5.-
  N3: PDH1.connector2, BLDC2.Vin+
  N4: PDH1.connector3, BLDC2.Vin-
  N5: PDH1.connector4, Kraken4.+
  N6: PDH1.connector5, Kraken4.-
  N7: PDH1.connector6, BLDC3.Vin+
  N8: PDH1.connector7, BLDC3.Vin-
  N9: PDH1.connector8, Vortex1.CAN-High2
  N10: PDH1.connector9, Vortex1.CAN-Low2
  N11: PDH1.connector10, Kraken3.+
  N12: PDH1.connector11, Kraken3.-
  N13: PDH1.connector12, Vortex2.CAN-High2
  N14: PDH1.connector13, Vortex2.CAN-Low2
  N15: PDH1.connector14, ctrl1.connector0
  N16: PDH1.connector15, ctrl1.connector1
  N17: PDH1.connector16, Kraken2.+
  N18: PDH1.connector17, Kraken2.-
  N19: PDH1.connector18, BLDC1.Vin+
  N20: PDH1.connector19, BLDC1.Vin-
  N21: PDH1.connector20, Kraken6.+
  N22: PDH1.connector21, Kraken6.-
  N23: PDH1.connector22, Falcon2.+
  N24: PDH1.connector23, Falcon2.-
  N25: PDH1.connector24, ctrl2.connector0
  N26: PDH1.connector25, ctrl2.connector1
  N27: PDH1.connector26, Kraken1.-
  N28: PDH1.connector27, Kraken1.+
  N29: PDH1.connector28, Vortex3.CAN-Low2
  N30: PDH1.connector29, Vortex3.CAN-High2
  N31: PDH1.connector30, switch1.pin7
  N32: PDH1.connector31, switch1.pin8
  N33: PDH1.connector32, Falcon3.-
  N34: PDH1.connector33, Falcon3.+
  N35: PDH1.connector34, Kraken8.-
  N36: PDH1.connector35, Kraken8.+
  N37: PDH1.connector36, Kraken7.-
  N38: PDH1.connector37, Kraken7.+
  N39: PDH1.connector38, Falcon1.-
  N40: PDH1.connector39, Falcon1.+
  N41: PDH1.connector44, JP2.1
  N42: PDH1.connector45, CB1.1
  N43: PDH1.connector46, cntl1.connector40
  N44: PDH1.connector47, cntl1.connector39
  N45: PDH1.connector48, Mini_Power_Module1.Input_-
  N46: PDH1.connector49, Mini_Power_Module1.Input_+
  N47: PDH1.connector50, RPM1.connector0
  N48: PDH1.connector51, RPM1.connector1
  N49: PDH1.connector52, J1.V-
  N50: PDH1.connector53, J1.V+
  N51: ctrl1.connector2, BLDC5.B
  N52: ctrl1.connector3, BLDC5.C
  N53: ctrl1.connector18, BLDC5.A
  N54: ctrl2.connector2, BLDC4.B
  N55: ctrl2.connector3, BLDC4.C
  N56: ctrl2.connector18, BLDC4.A
  N57: BAT1.+, JP1.2
  N58: BAT1.-, JP1.1
  N59: Mini_Power_Module1.4+, J3.pin_3
  N60: Mini_Power_Module1.4-, J3.pin2
  N61: Mini_Power_Module1.3-, BuckBoost1.in-
  N62: Mini_Power_Module1.2+, Part1.pin_3
  N63: Mini_Power_Module1.2-, Part1.pin_4
  N64: Mini_Power_Module1.1+, Pigeon_2_1.+
  N65: Mini_Power_Module1.1-, Pigeon_2_1.-
  N66: Mini_Power_Module1.0+, CANivore1.V+[R]
  N67: Mini_Power_Module1.0-, CANivore1.V-[B]
  N68: J2.DC-Power_+, BuckBoost1.out+
  N69: J2.DC-Power_-, BuckBoost1.out-
  N70: J3.pin1, J4.pin_35
  N71: CANcoder1.+, CANcoder3.+, Part1.pin1, Part2.pin_3, Part3.pin1, Part4.pin_3
  N72: CANcoder1.-, CANcoder3.-, Part1.pin2, Part2.pin_4, Part3.pin2, Part4.pin_4
  N73: CANcoder2.+, Part3.pin_3, Part4.pin1
  N74: CANcoder2.-, Part3.pin_4, Part4.pin2
  N75: CANcoder4.+, Part2.pin1
  N76: CANcoder4.-, Part2.pin2
  N77: JP2.2, CB1.2

custom parts:
  Kraken1: Kraken
  Kraken-Right: Kraken
  Falcon_Left1: Falcon
  CTRE Falcon 500: The Falcon 500 powered by Talon FX is a brushless motor with an integrated motor controller and high-resolution encoder, custom designed specifically for the FIRST Robotics Competition, through a collaboration between Cross the Road Electronics and VEX Robotics.
  REV NEO 550 BLDC Motor: The REV NEO 550 Brushless Motor is the newest member in the NEO family of brushless motors. Its output power and small size are specifically designed to make NEO 550 the perfect motor for intakes and other non-drivetrain robot mechanisms. Mounting holes and pilot match a standard 550 series motor, making it natively mount to many existing off-the-shelf gearboxes.
  Battery 12V: Battery Holders Various common sizes : AA, AAA, 20mm coin cell and 12mm coin cell.
  Generic female header - 2 pins: Generic female header
  REV Mini Power Module: Generic female header
  Generic female header - 5 pins: Generic female header
  CTRE Pigeon 2.0: Generic single row SMD female header
  APP SB50: Anderson Power Products SB®50 Connectors feature a one-piece plastic housing using stainless steel springs to hold low-resistance contacts in place. These connectors work with wire contacts up to 6AWG (10mm²) as well as PCB and busbar contacts. The genderless design mates with itself and has a plated through-hole mounting style. Anderson SB®50 Connectors are UL-rated for hot plugging up to 50A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
  Thermal Circuit Breaker: Cooper Bussman P/N CB185-120, CB185F-120, CB285-120 CB285F-120, CB285120F or Optifuse P/N 153120, 253120
