# Fritzing sketch 2025 Data Schematic (saved by Fritzing 1.0.2b)

parts:
  CANivore1 = CTRE CANivore [form="♀ (female)" package=THT]
  Kraken3 = Kraken- Left1
  Kraken4 = Kraken- Left1
  Kraken5 = Kraken- Left1
  Kraken6 = Kraken- Left1
  Pigeon_2_1 = CTRE Pigeon 2.0 [package=THT]
  cntl1 = roborio_v2
  switch4 = Network Switch
  J2 = Generic female header - 5 pins [form="♀ (female)" package=THT]
  RSL1 = FRC Robot Signal Light [part_number=855PB-B12ME522]
  J3 = Generic female header - 1 pins [form="♀ (female)" package=THT]
  J4 = Generic female header - 1 pins [form="♀ (female)" package=THT]
  RGB_Strip_LED17 = RGB Strip LED  # not connected
  RGB_Strip_LED18 = RGB Strip LED
  RGB_Strip_LED20 = RGB Strip LED  # not connected
  RGB_Strip_LED22 = RGB Strip LED  # not connected
  RGB_Strip_LED23 = RGB Strip LED  # not connected
  RGB_Strip_LED24 = RGB Strip LED  # not connected
  RGB_Strip_LED25 = RGB Strip LED  # not connected
  RGB_Strip_LED26 = RGB Strip LED
  RGB_Strip_LED27 = RGB Strip LED  # not connected
  RGB_Strip_LED28 = RGB Strip LED  # not connected
  RGB_Strip_LED29 = RGB Strip LED  # not connected
  RGB_Strip_LED30 = RGB Strip LED
  RGB_Strip_LED32 = RGB Strip LED  # not connected
  CANcoder3 = CTRE CANcoder [package=THT]
  CANcoder4 = CTRE CANcoder [package=THT]
  CANcoder7 = CTRE CANcoder [package=THT]
  CANcoder8 = CTRE CANcoder [package=THT]
  Kraken18 = Kraken- Left1
  Kraken19 = Kraken- Left1
  CANcoder10 = CTRE CANcoder [package=THT]
  Kraken22 = Kraken- Left1
  Kraken23 = Kraken- Left1
  Kraken24 = Kraken- Left1
  Kraken25 = Kraken- Left1
  CANcoder11 = CTRE CANcoder [package=THT]
  CANrange1 = CTRE CANrange [package=THT]
  CANrange2 = CTRE CANrange [package=THT]
  R1 = Resistor [tolerance=±5% power=0.25W resistance=120 package=THT]
  Kraken26 = Kraken- Left1
  Kraken27 = Kraken- Left1
  J12 = Generic female header - 2 pins [form="♀ (female)" package=THT]
  J13 = Generic female header - 2 pins [form="♀ (female)" package=THT]
  Kraken31 = Kraken- Left1
  CANcoder13 = CTRE CANcoder [package=THT]
  Kraken17 = Kraken- Left1
  Kraken30 = Kraken- Left1
  CANcoder14 = CTRE CANcoder [package=THT]
  RGB_Strip_LED33 = RGB Strip LED  # not connected
  Kraken32 = Kraken-Right

nets:
  N1: CANivore1.CANL[G], Pigeon_2_1.IN-CANH[Y]
  N2: CANivore1.CANH[Y], Pigeon_2_1.IN-CANL[G]
  N3: CANivore1.USB-C, cntl1.connector142
  N4: Kraken3.CAN_High_1, CANcoder3.OUT-CANH[Y]
  N5: Kraken3.CAN_Low_1, CANcoder3.OUT-CANL[G]
  N6: Kraken3.CAN_High_2, CANcoder7.OUT-CANH[Y]
  N7: Kraken3.CAN_Low_2, CANcoder7.OUT-CANL[G]
  N8: Kraken4.CAN_High_1, Kraken26.CAN_High_2
  N9: Kraken4.CAN_Low_1, Kraken26.CAN_Low_2
  N10: Kraken4.CAN_High_2, CANcoder3.IN-CANH[Y]
  N11: Kraken4.CAN_Low_2, CANcoder3.IN-CANL[G]
  N12: Kraken5.CAN_High_1, CANcoder4.OUT-CANH[Y]
  N13: Kraken5.CAN_Low_1, CANcoder4.OUT-CANL[G]
  N14: Kraken5.CAN_High_2, Kraken27.CAN_High_1
  N15: Kraken5.CAN_Low_2, Kraken27.CAN_Low_1
  N16: Kraken6.CAN_High_1, Kraken18.CAN_High_2
  N17: Kraken6.CAN_Low_1, Kraken18.CAN_Low_2
  N18: Kraken6.CAN_High_2, CANcoder4.IN-CANH[Y]
  N19: Kraken6.CAN_Low_2, CANcoder4.IN-CANL[G]
  N20: Pigeon_2_1.OUT-CANH[Y], CANcoder8.IN-CANL[G]
  N21: Pigeon_2_1.OUT-CANL[G], CANcoder8.IN-CANH[Y]
  N22: cntl1.connector33, J12.-
  N23: cntl1.connector35, J12.+
  N24: cntl1.connector36, J13.-
  N25: cntl1.connector38, J13.+
  N26: cntl1.connector41, RSL1.anode1
  N27: cntl1.connector42, RSL1.common_cathode
  N28: cntl1.connector138, RGB_Strip_LED30.Green_Connect
  N29: cntl1.connector144, switch4.RIO
  N30: switch4.AUX_1, J2.Ethernet
  N31: J2.USB-3, J3.pin1
  N32: J2.USB-4, J4.pin1
  N33: RGB_Strip_LED18.Green_Connect, RGB_Strip_LED26.Green_Connect
  N34: CANcoder7.IN-CANH[Y], CANcoder8.OUT-CANH[Y]
  N35: CANcoder7.IN-CANL[G], CANcoder8.OUT-CANL[G]
  N36: Kraken18.CAN_High_1, CANcoder14.OUT-CANH[Y]
  N37: Kraken18.CAN_Low_1, CANcoder14.OUT-CANL[G]
  N38: Kraken19.CAN_High_1, Kraken23.CAN_High_2
  N39: Kraken19.CAN_Low_1, Kraken23.CAN_Low_2
  N40: Kraken19.CAN_High_2, CANcoder10.IN-CANH[Y]
  N41: Kraken19.CAN_Low_2, CANcoder10.IN-CANL[G]
  N42: CANcoder10.OUT-CANH[Y], Kraken17.CAN_High_1, Kraken30.CAN_High_1
  N43: CANcoder10.OUT-CANL[G], Kraken30.CAN_Low_1
  N44: Kraken22.CAN_High_1, CANcoder11.OUT-CANH[Y]
  N45: Kraken22.CAN_Low_1, CANcoder11.OUT-CANL[G]
  N46: Kraken22.CAN_High_2, Kraken24.CAN_High_1
  N47: Kraken22.CAN_Low_2, Kraken24.CAN_Low_1
  N48: Kraken23.CAN_High_1, Kraken24.CAN_High_2
  N49: Kraken23.CAN_Low_1, Kraken24.CAN_Low_2
  N50: Kraken25.CAN_High_1, Kraken32.CAN-High2
  N51: Kraken25.CAN_Low_1, Kraken32.CAN_Low2
  N52: Kraken25.CAN_High_2, CANcoder11.IN-CANH[Y]
  N53: Kraken25.CAN_Low_2, CANcoder11.IN-CANL[G]
  N54: CANrange1.CANH[Y], CANrange2.CANH[Y], R1.Pin_1, Kraken32.CAN_High1
  N55: CANrange1.CANL[G], CANrange2.CANL[G], R1.Pin_0, Kraken32.CAN_Low1
  N56: Kraken26.CAN_High_1, Kraken27.CAN_High_2
  N57: Kraken26.CAN_Low_1, Kraken27.CAN_Low_2
  N58: Kraken31.CAN_High_1, CANcoder13.OUT-CANH[Y]
  N59: Kraken31.CAN_Low_1, CANcoder13.OUT-CANL[G]
  N60: Kraken31.CAN_High_2, CANcoder14.IN-CANH[Y]
  N61: Kraken31.CAN_Low_2, CANcoder14.IN-CANL[G]
  N62: CANcoder13.IN-CANH[Y], Kraken17.CAN_Low_1, Kraken30.CAN_High_2
  N63: CANcoder13.IN-CANL[G], Kraken17.CAN_High_2, Kraken30.CAN_Low_2

custom parts:
  Kraken- Left1: Kraken
  CTRE Pigeon 2.0: Generic single row SMD female header
  Generic female header - 5 pins: Generic female header
  FRC Robot Signal Light: Panel Mount Beacon,12V AC/DC,45 mm Panel Mounting LED,Amber,22.5 mm Round Mounting Hole Used as: R709 *ROBOTS must have a signal light. ROBOTS must use at least 1, but no more than 2, diagnostic ROBOT Signal Light (RSL) (P/N 855PB-B12ME522). Any RSL must be: A. mounted on the ROBOT such that it is easily visible while standing 3 ft. (~ 100 cm) in front of the ROBOT, B. connected to the “RSL”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
  Generic female header - 1 pins: Generic female header
  RGB Strip LED: A tri-color Strip LED with red, green and blue. Based on LED SMD 5050 RGB Pin order: common cathode - green - red - blue
  Generic female header - 2 pins: Generic female header
  Kraken-Right: Kraken
