# Fritzing sketch 2025 Power Schematic (saved by Fritzing 1.0.2b)

parts:
  PDH1 = rev_pdh
  Kraken1 = Kraken-Right
  Kraken2 = Kraken-Right
  Kraken4 = Kraken-Right
  Kraken5 = Kraken-Right
  Kraken6 = Kraken- Left1
  Kraken7 = Kraken- Left1
  Kraken8 = Kraken- Left1
  Kraken9 = Kraken- Left1
  F1 = Resettable Fuse PTC [package=0603]  # not connected
  F2 = Resettable Fuse PTC [package=0603]  # not connected
  F3 = Resettable Fuse PTC [package=0603]  # not connected
  F4 = Resettable Fuse PTC [package=0603]  # not connected
  F5 = Resettable Fuse PTC [package=0603]  # not connected
  F6 = Resettable Fuse PTC [package=0603]  # not connected
  F7 = Resettable Fuse PTC [package=0603]  # not connected
  F8 = Resettable Fuse PTC [package=0603]  # not connected
  CB1 = Thermal Circuit Breaker [package=waterproof]
  BAT1 = Battery 12V [package=battcom_20mm_pth]
  F9 = Resettable Fuse PTC [package=0603]  # not connected
  F10 = Resettable Fuse PTC [package=0603]  # not connected
  F11 = Resettable Fuse PTC [package=0603]  # not connected
  F12 = Resettable Fuse PTC [package=0603]  # not connected
  F13 = Resettable Fuse PTC [package=0603]  # not connected
  F14 = Resettable Fuse PTC [package=0603]  # not connected
  F15 = Resettable Fuse PTC [package=0603]  # not connected
  F16 = Resettable Fuse PTC [package=0603]  # not connected
  Kraken10 = Kraken- Left1
  Kraken12 = Kraken- Left1
  Kraken13 = Kraken- Left1
  Kraken14 = Kraken-Right
  Kraken15 = Kraken-Right
  Kraken16 = Kraken-Right
  Kraken17 = Kraken-Right
  F17 = Resettable Fuse PTC [package=0603]  # not connected
  F18 = Resettable Fuse PTC [package=0603]  # not connected
  Kraken11 = Kraken- Left1
  Mini_Power_Module1 = REV Mini Power Module [form="♀ (female)" package=THT]
  cntl1 = roborio_v2
  DC1 = Pololu reg29b 0J14085 Voltage Regulator
  J1 = Generic female header - 5 pins [form="♀ (female)" package=THT]
  Part3 = Wago 222
  CANivore1 = CTRE CANivore [form="♀ (female)" package=THT]
  Pigeon_2_1 = CTRE Pigeon 2.0 [package=THT]
  Part4 = Wago 222
  Part5 = Wago 222
  Part6 = Wago 222
  Part7 = Wago 222
  F19 = Resettable Fuse PTC [package=0603]  # not connected
  F20 = Resettable Fuse PTC [package=0603]  # not connected
  F21 = Resettable Fuse PTC [package=0603]  # not connected
  F22 = Resettable Fuse PTC [package=0603]  # not connected
  F23 = Resettable Fuse PTC [package=0603]  # not connected
  F24 = Resettable Fuse PTC [package=0603]  # not connected
  F25 = Resettable Fuse PTC [package=0603]  # not connected
  F26 = Resettable Fuse PTC [package=0603]  # not connected
  F27 = Resettable Fuse PTC [package=0603]  # not connected
  F28 = Resettable Fuse PTC [package=0603]  # not connected
  F29 = Resettable Fuse PTC [package=0603]  # not connected
  F30 = Resettable Fuse PTC [package=0603]  # not connected
  F31 = Resettable Fuse PTC [package=0603]  # not connected
  F32 = Resettable Fuse PTC [package=0603]  # not connected
  Part8 = Wago 222
  Part9 = Wago 222
  JP2 = APP SB50 [package=sb50]
  JP3 = APP SB50 [package=sb50]
  CANcoder1 = CTRE CANcoder [package=THT]
  CANcoder2 = CTRE CANcoder [package=THT]
  CANcoder3 = CTRE CANcoder [package=THT]
  CANcoder4 = CTRE CANcoder [package=THT]
  CANcoder5 = CTRE CANcoder [package=THT]
  CANcoder6 = CTRE CANcoder [package=THT]
  switch1 = Network Switch
  RGB_Strip_LED1 = RGB Strip LED  # not connected
  RGB_Strip_LED2 = RGB Strip LED  # not connected
  RGB_Strip_LED3 = RGB Strip LED  # not connected
  RGB_Strip_LED4 = RGB Strip LED  # not connected
  RGB_Strip_LED5 = RGB Strip LED  # not connected
  RGB_Strip_LED6 = RGB Strip LED
  RGB_Strip_LED7 = RGB Strip LED  # not connected
  RGB_Strip_LED8 = RGB Strip LED  # not connected
  RGB_Strip_LED9 = RGB Strip LED  # not connected
  RGB_Strip_LED10 = RGB Strip LED  # not connected
  RGB_Strip_LED11 = RGB Strip LED  # not connected
  RGB_Strip_LED12 = RGB Strip LED  # not connected
  RGB_Strip_LED13 = RGB Strip LED  # not connected
  RGB_Strip_LED14 = RGB Strip LED  # not connected
  RGB_Strip_LED15 = RGB Strip LED  # not connected
  RGB_Strip_LED16 = RGB Strip LED  # not connected

nets:
  N1: PDH1.connector0, PDH1.connector4, Kraken4.+, Kraken14.+
  N2: PDH1.connector1, PDH1.connector5, Kraken4.-, Kraken14.-
  N3: PDH1.connector2, PDH1.connector6, Kraken5.+, Kraken15.+
  N4: PDH1.connector3, PDH1.connector7, Kraken5.-, Kraken15.-
  N5: PDH1.connector8, PDH1.connector16, Kraken2.+, Kraken17.+
  N6: PDH1.connector9, PDH1.connector17, Kraken2.-, Kraken17.-
  N7: PDH1.connector10, PDH1.connector18, Kraken1.+, Kraken16.+
  N8: PDH1.connector11, PDH1.connector19, Kraken1.-, Kraken16.-
  N9: PDH1.connector20, PDH1.connector29, Kraken6.+, Kraken12.+
  N10: PDH1.connector21, PDH1.connector28, Kraken6.-, Kraken12.-
  N11: PDH1.connector22, Kraken7.+
  N12: PDH1.connector23, Kraken7.-
  N13: PDH1.connector30, Kraken13.-
  N14: PDH1.connector31, Kraken13.+
  N15: PDH1.connector32, PDH1.connector36, Kraken9.-, Kraken11.-
  N16: PDH1.connector33, PDH1.connector37, Kraken9.+, Kraken11.+
  N17: PDH1.connector34, PDH1.connector38, Kraken8.-, Kraken10.-
  N18: PDH1.connector35, PDH1.connector39, Kraken8.+, Kraken10.+
  N19: PDH1.connector44, JP3.1
  N20: PDH1.connector45, CB1.1
  N21: PDH1.connector46, Mini_Power_Module1.Input_-
  N22: PDH1.connector47, Mini_Power_Module1.Input_+
  N23: PDH1.connector48, cntl1.connector40
  N24: PDH1.connector49, cntl1.connector39
  N25: CB1.2, JP3.2
  N26: BAT1.+, JP2.2
  N27: BAT1.-, JP2.1
  N28: Mini_Power_Module1.5+, DC1.IN+
  N29: Mini_Power_Module1.5-, DC1.IN-
  N30: Mini_Power_Module1.4+, RGB_Strip_LED6.Common_Connect
  N31: Mini_Power_Module1.4-, RGB_Strip_LED6.Blue_Connect
  N32: Mini_Power_Module1.3+, switch1.12v_-
  N33: Mini_Power_Module1.3-, switch1.12v_+
  N34: Mini_Power_Module1.1+, Part4.pin2
  N35: Mini_Power_Module1.1-, Part4.pin1
  N36: Mini_Power_Module1.0+, Part3.pin2
  N37: Mini_Power_Module1.0-, Part3.pin1
  N38: DC1.OUT+, DC1.OUT-, J1.DC-Power_In
  N39: Part3.pin_3, CANivore1.V-[B], Pigeon_2_1.-
  N40: Part3.pin_4, CANivore1.V+[R], Pigeon_2_1.+
  N41: Part4.pin_3, Part5.pin1, CANcoder6.-
  N42: Part4.pin_4, Part5.pin2, CANcoder6.+
  N43: Part5.pin_3, Part6.pin1, CANcoder5.-
  N44: Part5.pin_4, Part6.pin2, CANcoder5.+
  N45: Part6.pin_3, Part7.pin1, CANcoder4.-
  N46: Part6.pin_4, Part7.pin2, CANcoder4.+
  N47: Part7.pin_3, Part8.pin1, CANcoder3.-
  N48: Part7.pin_4, Part8.pin2, CANcoder3.+
  N49: Part8.pin_3, Part9.pin1, CANcoder2.-
  N50: Part8.pin_4, Part9.pin2, CANcoder2.+
  N51: Part9.pin_3, CANcoder1.-
  N52: Part9.pin_4, CANcoder1.+

custom parts:
  Kraken-Right: Kraken
  Kraken- Left1: Kraken
  Resettable Fuse PTC: Resettable Fuse PTC Resettable Fuse. Spark Fun Electronics SKU : COM-08357
  Thermal Circuit Breaker: Cooper Bussman P/N CB185-120, CB185F-120, CB285-120 CB285F-120, CB285120F or Optifuse P/N 153120, 253120
  Battery 12V: Battery Holders Various common sizes : AA, AAA, 20mm coin cell and 12mm coin cell.
  Resettable Fuse PTC: Resettable Fuse PTC Resettable Fuse. Spark Fun Electronics SKU : COM-08357
  Resettable Fuse PTC: Resettable Fuse PTC Resettable Fuse. Spark Fun Electronics SKU : COM-08357
  REV Mini Power Module: Generic female header
  Generic female header - 5 pins: Generic female header
  CTRE Pigeon 2.0: Generic single row SMD female header
  APP SB50: Anderson Power Products SB®50 Connectors feature a one-piece plastic housing using stainless steel springs to hold low-resistance contacts in place. These connectors work with wire contacts up to 6AWG (10mm²) as well as PCB and busbar contacts. The genderless design mates with itself and has a plated through-hole mounting style. Anderson SB®50 Connectors are UL-rated for hot plugging up to 50A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
  RGB Strip LED: A tri-color Strip LED with red, green and blue. Based on LED SMD 5050 RGB Pin order: common cathode - green - red - blue
