# Fritzing sketch 2026 Power Wiring Diagram (saved by Fritzing 1.0.2b)

parts:
  PDH1 = 2026PDH
  cntl1 = roborio_v2
  switch1 = Network Switch
  Front_Left_Drive = Kraken-Right
  Front_Right_Drive = Kraken-Right
  Back_Right_Drive = Kraken- Left1
  Back_left_Drive = Kraken- Left1
  Shooter_2 = Kraken-Right
  Intake_2 = Kraken-Right
  Shooter_1 = Kraken- Left1
  Intake_1 = Kraken- Left1
  Part1 = Arduino Nano (Rev3.0)
  Intake_3 = Kraken-Right
  U1 = Nokia 6100 Color LCD [package=nokia6100_lcd]
  Kraken1 = Kraken-Right
  Kraken2 = Kraken-Right
  Kraken3 = Kraken-Right
  Kraken4 = Kraken-Right
  Part2 = Arduino Mega 2560 (Rev3)
  Mini_Power_Module1 = REV Mini Power Module [form="♀ (female)" package=THT]
  Pigeon_2_1 = CTRE Pigeon 2.0 [package=THT]
  CANivore1 = CTRE CANivore [form="♀ (female)" package=THT]
  CANcoder1 = CTRE CANcoder [package=THT]
  CANcoder2 = CTRE CANcoder [package=THT]
  CANcoder3 = CTRE CANcoder [package=THT]
  CANcoder4 = CTRE CANcoder [package=THT]
  Kraken5 = Kraken- Left1
  RSL1 = FRC Robot Signal Light [part_number=855PB-B12ME522]

nets:
  N1: PDH1.connector0, Intake_3.+
  N2: PDH1.connector1, Intake_3.-
  N3: PDH1.connector2, Kraken4.+, CANcoder4.+
  N4: PDH1.connector3, Kraken4.-, CANcoder4.-
  N5: PDH1.connector4, Back_Right_Drive.+
  N6: PDH1.connector5, Back_Right_Drive.-
  N7: PDH1.connector6, Kraken3.+, CANcoder3.+
  N8: PDH1.connector7, Kraken3.-, CANcoder3.-
  N9: PDH1.connector8, Back_left_Drive.+
  N10: PDH1.connector9, Back_left_Drive.-
  N11: PDH1.connector10, Kraken2.+, CANcoder2.+
  N12: PDH1.connector11, Kraken2.-, CANcoder2.-
  N13: PDH1.connector12, Front_Right_Drive.+
  N14: PDH1.connector13, Front_Right_Drive.-
  N15: PDH1.connector14, Kraken1.+, CANcoder1.+
  N16: PDH1.connector15, Kraken1.-, CANcoder1.-
  N17: PDH1.connector16, Front_Left_Drive.+
  N18: PDH1.connector17, Front_Left_Drive.-
  N19: PDH1.connector20, Mini_Power_Module1.Input_+
  N20: PDH1.connector21, Mini_Power_Module1.Input_-
  N21: PDH1.connector22, cntl1.connector39
  N22: PDH1.connector23, cntl1.connector40
  N23: PDH1.connector24, switch1.12v_+
  N24: PDH1.connector25, switch1.12v_-
  N25: PDH1.connector26, Part1.V-
  N26: PDH1.connector27, Part1.V+
  N27: PDH1.connector28, U1.V-#8
  N28: PDH1.connector29, U1.V+#7
  N29: PDH1.connector30, Shooter_1.-
  N30: PDH1.connector31, Shooter_1.+
  N31: PDH1.connector32, Shooter_2.-
  N32: PDH1.connector33, Shooter_2.+
  N33: PDH1.connector34, Kraken5.-
  N34: PDH1.connector35, Kraken5.+
  N35: PDH1.connector50, Intake_1.-
  N36: PDH1.connector51, Intake_1.+
  N37: PDH1.connector52, Intake_2.-
  N38: PDH1.connector53, Intake_2.+
  N39: cntl1.connector41, RSL1.anode0
  N40: cntl1.connector42, RSL1.common_cathode
  N41: U1.V+#0, Part2.V+
  N42: U1.V-#1, Part2.V-
  N43: Mini_Power_Module1.2+, Pigeon_2_1.+
  N44: Mini_Power_Module1.2-, Pigeon_2_1.-
  N45: Mini_Power_Module1.1+, CANivore1.V+[R]
  N46: Mini_Power_Module1.1-, CANivore1.V-[B]

notes:
  Represents 4 Motors

custom parts:
  Kraken-Right: Kraken
  Kraken- Left1: Kraken
  Arduino Nano (Rev3.0): The Arduino Nano is a small, complete, and breadboard-friendly board based on the ATmega328 (Arduino Nano 3.0) or ATmega168 (Arduino Nano 2.x). It has more or less the same functionality of the Arduino Duemilanove, but in a different package. It lacks only a DC power jack, and works with a Mini-B USB cable instead of a standard one. The Nano was designed and is being produced by Gravitech.
  Nokia 6100 Color LCD: Nokia 6100 Color LCD Schematic element and footprint production proven but could use some touching up. Spark Fun Electronics SKU : LCD-00569. Mating SMD connector : LCD-00570
  Kraken-Right: Kraken
  Arduino Mega 2560 (Rev3): The Arduino Mega 2560 is a microcontroller board based on the ATmega2560 (datasheet). It has 54 digital input/output pins (of which 14 can be used as PWM outputs), 16 analog inputs, 4 UARTs (hardware serial ports), a 16 MHz crystal oscillator, a USB connection, a power jack, an ICSP header, and a reset button. It contains everything needed to support the microcontroller; simply connect it to a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
  REV Mini Power Module: Generic female header
  CTRE Pigeon 2.0: Generic single row SMD female header
  Kraken- Left1: Kraken
  FRC Robot Signal Light: Panel Mount Beacon,12V AC/DC,45 mm Panel Mounting LED,Amber,22.5 mm Round Mounting Hole Used as: R709 *ROBOTS must have a signal light. ROBOTS must use at least 1, but no more than 2, diagnostic ROBOT Signal Light (RSL) (P/N 855PB-B12ME522). Any RSL must be: A. mounted on the ROBOT such that it is easily visible while standing 3 ft. (~ 100 cm) in front of the ROBOT, B. connected to the “RSL”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
