# Fritzing sketch 2026 Data schmatic (saved by Fritzing 1.0.2b)

parts:
  cntl1 = roborio_v2
  CANivore1 = CTRE CANivore [form="♀ (female)" package=THT]
  Pigeon_2_1 = CTRE Pigeon 2.0 [package=THT]
  Kraken2 = Kraken- Left1  # not connected
  CANcoder1 = CTRE CANcoder [package=THT]
  Kraken3 = Kraken- Left1  # not connected
  Kraken4 = Kraken- Left1
  Kraken5 = Kraken- Left1
  Kraken6 = Kraken- Left1
  CANcoder2 = CTRE CANcoder [package=THT]
  Kraken7 = Kraken- Left1
  Kraken8 = Kraken-Right
  Kraken9 = Kraken- Left1
  Kraken10 = Kraken- Left1
  CANcoder3 = CTRE CANcoder [package=THT]
  switch1 = Network Switch
  Kraken11 = Kraken- Left1  # not connected
  Kraken12 = Kraken- Left1  # not connected
  Part1 = Arduino Nano (Rev3.0)
  S1 = Round Pushbutton
  Kraken13 = Kraken- Left1
  Kraken14 = Kraken- Left1
  CANcoder4 = CTRE CANcoder [package=THT]
  Kraken15 = Kraken- Left1  # not connected
  Kraken16 = Kraken- Left1
  Kraken17 = Kraken- Left1
  Kraken18 = Kraken- Left1
  R1 = Resistor [tolerance=±5% power=0.25W resistance=220 package=THT]
  U1 = Nokia 6100 Color LCD [package=nokia6100_lcd]  # not connected
  switch2 = Network Switch  # not connected
  J1 = Generic female header - 1 pins [form="♀ (female)" package=THT]  # not connected
  J2 = Generic female header - 1 pins [form="♀ (female)" package=THT]  # not connected
  J3 = Generic female header - 1 pins [form="♀ (female)" package=THT]  # not connected

nets:
  N1: cntl1.connector142, CANivore1.USB-C
  N2: cntl1.connector144, switch1.RIO
  N3: CANivore1.CANL[G], Pigeon_2_1.IN-CANH[Y]
  N4: CANivore1.CANH[Y], Pigeon_2_1.IN-CANL[G]
  N5: CANcoder1.OUT-CANH[Y], Kraken4.CAN_High_1
  N6: CANcoder1.OUT-CANL[G], Kraken4.CAN_Low_1
  N7: Kraken5.CAN_High_1, CANcoder2.IN-CANL[G]
  N8: Kraken5.CAN_Low_1, CANcoder2.IN-CANH[Y]
  N9: Kraken6.CAN_Low_1, CANcoder2.OUT-CANL[G]
  N10: Kraken6.-, CANcoder2.OUT-CANH[Y]
  N11: Kraken7.CAN_High_1, Kraken9.CAN_High_2
  N12: Kraken7.CAN_Low_1, Kraken9.CAN_Low_2
  N13: Kraken7.CAN_High_2, Kraken8.CAN-High2
  N14: Kraken7.CAN_Low_2, Kraken8.CAN_Low2
  N15: Kraken9.CAN_High_1, CANcoder3.IN-CANL[G]
  N16: Kraken9.CAN_Low_1, CANcoder3.IN-CANH[Y]
  N17: Kraken10.CAN_Low_1, CANcoder3.OUT-CANH[Y]
  N18: Kraken10.-, CANcoder3.OUT-CANL[G]
  N19: Part1.S1In, S1.leg0
  N20: Part1.V-Out, S1.leg1
  N21: Kraken13.CAN_High_1, CANcoder4.IN-CANH[Y]
  N22: Kraken13.CAN_Low_1, CANcoder4.IN-CANL[G]
  N23: Kraken14.CAN_High_1, CANcoder4.OUT-CANH[Y]
  N24: Kraken14.CAN_Low_1, CANcoder4.OUT-CANL[G]
  N25: Kraken16.CAN_High_1, Kraken17.CAN_High_2
  N26: Kraken16.CAN_Low_1, Kraken17.CAN_Low_2
  N27: Kraken17.CAN_High_1, Kraken18.CAN_High_1, R1.Pin_0
  N28: Kraken17.CAN_Low_1, R1.Pin_1

custom parts:
  CTRE Pigeon 2.0: Generic single row SMD female header
  Kraken- Left1: Kraken
  Kraken- Left1: Kraken
  Kraken-Right: Kraken
  Arduino Nano (Rev3.0): The Arduino Nano is a small, complete, and breadboard-friendly board based on the ATmega328 (Arduino Nano 3.0) or ATmega168 (Arduino Nano 2.x). It has more or less the same functionality of the Arduino Duemilanove, but in a different package. It lacks only a DC power jack, and works with a Mini-B USB cable instead of a standard one. The Nano was designed and is being produced by Gravitech.
  Nokia 6100 Color LCD: Nokia 6100 Color LCD Schematic element and footprint production proven but could use some touching up. Spark Fun Electronics SKU : LCD-00569. Mating SMD connector : LCD-00570
  Generic female header - 1 pins: Generic female header
